// Logisim project Trabalho.circ as structural Verilog: 20 circuits, main circuit alu_8_bits
module alu_8_bits (
  input  [7:0] A,
  input  [7:0] B,
  input  Cin,
  input  [2:0] OP,
  output C,
  output z,
  output [7:0] s
);

  wire decodificador_4_b_1_a, decodificador_4_b_1_b, decodificador_4_b_1_c, decodificador_4_b_1_d,
       decodificador_4_b_1_e, decodificador_4_b_1_f, decodificador_4_b_1_g, decodificador_4_b_2_a,
       decodificador_4_b_2_b, decodificador_4_b_2_c, decodificador_4_b_2_d, decodificador_4_b_2_e,
       decodificador_4_b_2_f, decodificador_4_b_2_g, shift_left_8_bits_1_cout, shift_right_8_bits_1_cout,
       somador_8_bits_1_cout, subtracao_8_bits_1_cout;
  wire [7:0] and_8_bits_1_s, or_8_bits_1_s, shift_left_8_bits_1_s, shift_right_8_bits_1_s,
       somador_8_bits_1_s, subtracao_8_bits_1_s, xor_8_bits_1_s;

  Decodificador_Carry decodificador_carry_1 (
    .OP(OP), .SHR(shift_right_8_bits_1_cout), .ADD(somador_8_bits_1_cout), .SUB(subtracao_8_bits_1_cout),
    .SHL(shift_left_8_bits_1_cout), .C(C));
  somador_8_bits somador_8_bits_1 (.S(somador_8_bits_1_s), .Cout(somador_8_bits_1_cout), .A(A), .B(B), .Cin(Cin));
  Subtracao_8_bits subtracao_8_bits_1 (
    .S(subtracao_8_bits_1_s), .Cout(subtracao_8_bits_1_cout), .A(A), .B(B), .Cin(Cin));
  MUL_8_1_8bits mul_8_1_8bits_1 (
    .CHOR(xor_8_bits_1_s), .OP(OP), .OU(and_8_bits_1_s), .XXX({8{1'b0}}), .E(or_8_bits_1_s),
    .SHR(shift_right_8_bits_1_s), .SHL(shift_left_8_bits_1_s), .SUB(subtracao_8_bits_1_s),
    .ADD(somador_8_bits_1_s), .S(s));
  Shift_Left_8_bits shift_left_8_bits_1 (.B(A), .S(shift_left_8_bits_1_s), .Cout(shift_left_8_bits_1_cout), .Cin(Cin));
  Shift_Right_8_bits shift_right_8_bits_1 (
    .B(A), .S(shift_right_8_bits_1_s), .Cout(shift_right_8_bits_1_cout), .Cin(Cin));
  AND_8_bits and_8_bits_1 (.S(and_8_bits_1_s), .A(A), .B(B));
  XOR_8_bits xor_8_bits_1 (.S(xor_8_bits_1_s), .A(A), .B(B));
  OR_8_bits or_8_bits_1 (.S(or_8_bits_1_s), .A(A), .B(B));
  Igual_0_8b igual_0_8b_1 (.a(s), .s(z));
  Decodificador_4_b decodificador_4_b_1 (
    .a0(s[7]), .a1(s[6]), .a2(s[5]), .a3(s[4]), .a(decodificador_4_b_1_a), .b(decodificador_4_b_1_b),
    .c(decodificador_4_b_1_c), .d(decodificador_4_b_1_d), .e(decodificador_4_b_1_e),
    .f(decodificador_4_b_1_f), .g(decodificador_4_b_1_g));
  Decodificador_4_b decodificador_4_b_2 (
    .a0(s[3]), .a1(s[2]), .a2(s[1]), .a3(s[0]), .a(decodificador_4_b_2_a), .b(decodificador_4_b_2_b),
    .c(decodificador_4_b_2_c), .d(decodificador_4_b_2_d), .e(decodificador_4_b_2_e),
    .f(decodificador_4_b_2_f), .g(decodificador_4_b_2_g));
  _7_Segment_Display u_7_segment_display_1 (
    .g(decodificador_4_b_1_g), .f(decodificador_4_b_1_f), .a(decodificador_4_b_1_a),
    .b(decodificador_4_b_1_b), .e(decodificador_4_b_1_e), .d(decodificador_4_b_1_d), .c(decodificador_4_b_1_c));  // open: dp
  _7_Segment_Display u_7_segment_display_2 (
    .g(decodificador_4_b_2_g), .f(decodificador_4_b_2_f), .a(decodificador_4_b_2_a),
    .b(decodificador_4_b_2_b), .e(decodificador_4_b_2_e), .d(decodificador_4_b_2_d), .c(decodificador_4_b_2_c));  // open: dp
endmodule

module alu_16_bits (
  input  [15:0] A,
  input  [15:0] B,
  input  [2:0] OP,
  output [15:0] S,
  output Z,
  output Cout
);

  wire alu_8_bits_1_c, alu_8_bits_1_z, alu_8_bits_2_z;

  alu_8_bits alu_8_bits_1 (
    .A(A[7:0]), .B(B[7:0]), .OP(OP), .s(S[7:0]), .z(alu_8_bits_1_z), .Cin(Cout), .C(alu_8_bits_1_c));
  alu_8_bits alu_8_bits_2 (
    .A(A[15:8]), .B(B[15:8]), .OP(OP), .s(S[15:8]), .z(alu_8_bits_2_z), .Cin(alu_8_bits_1_c), .C(Cout));
  and and_1 (Z, alu_8_bits_1_z, alu_8_bits_2_z);
endmodule

module OR_8_bits (
  input  [7:0] A,
  input  [7:0] B,
  output [7:0] S
);

  or or_1 (S[7], A[7], B[7]);
  or or_2 (S[6], A[6], B[6]);
  or or_3 (S[4], A[4], B[4]);
  or or_4 (S[5], A[5], B[5]);
  or or_5 (S[3], A[3], B[3]);
  or or_6 (S[2], A[2], B[2]);
  or or_7 (S[0], A[0], B[0]);
  or or_8 (S[1], A[1], B[1]);
endmodule

module OR_8_bits_7x (
  input  [7:0] s1,
  input  [7:0] s2,
  input  [7:0] s3,
  input  [7:0] s4,
  input  [7:0] s5,
  input  [7:0] s6,
  input  [7:0] s7,
  output [7:0] s
);

  wire [7:0] or_8_bits_2_s, or_8_bits_3_s, or_8_bits_4_s, or_8_bits_5_s, or_8_bits_6_s;

  OR_8_bits or_8_bits_1 (.S(s), .A(or_8_bits_2_s), .B(or_8_bits_5_s));
  OR_8_bits or_8_bits_2 (.S(or_8_bits_2_s), .A(or_8_bits_4_s), .B(or_8_bits_3_s));
  OR_8_bits or_8_bits_3 (.S(or_8_bits_3_s), .A(s2), .B(s6));
  OR_8_bits or_8_bits_4 (.S(or_8_bits_4_s), .A(s1), .B(s5));
  OR_8_bits or_8_bits_5 (.S(or_8_bits_5_s), .A(or_8_bits_6_s), .B(s4));
  OR_8_bits or_8_bits_6 (.S(or_8_bits_6_s), .A(s3), .B(s7));
endmodule

module AND_8_bits (
  input  [7:0] A,
  input  [7:0] B,
  output [7:0] S
);

  and and_1 (S[7], A[7], B[7]);
  and and_2 (S[6], A[6], B[6]);
  and and_3 (S[4], A[4], B[4]);
  and and_4 (S[5], A[5], B[5]);
  and and_5 (S[3], A[3], B[3]);
  and and_6 (S[2], A[2], B[2]);
  and and_7 (S[1], A[1], B[1]);
  and and_8 (S[0], A[0], B[0]);
endmodule

module XOR_2_bits (
  input  A,
  input  B,
  output S
);

  wire and_1_out, and_2_out, not_1_out, not_2_out;

  not not_1 (not_1_out, A);
  not not_2 (not_2_out, B);
  and and_1 (and_1_out, not_1_out, B);
  and and_2 (and_2_out, A, not_2_out);
  or or_1 (S, and_1_out, and_2_out);
endmodule

module XOR_8_bits (
  input  [7:0] A,
  input  [7:0] B,
  output [7:0] S
);

  XOR_2_bits xor_2_bits_1 (.A(A[7]), .B(B[7]), .S(S[7]));
  XOR_2_bits xor_2_bits_2 (.A(A[6]), .B(B[6]), .S(S[6]));
  XOR_2_bits xor_2_bits_3 (.A(A[4]), .B(B[4]), .S(S[4]));
  XOR_2_bits xor_2_bits_4 (.A(A[5]), .B(B[5]), .S(S[5]));
  XOR_2_bits xor_2_bits_5 (.A(A[3]), .B(B[3]), .S(S[3]));
  XOR_2_bits xor_2_bits_6 (.A(A[2]), .B(B[2]), .S(S[2]));
  XOR_2_bits xor_2_bits_7 (.A(A[0]), .B(B[0]), .S(S[0]));
  XOR_2_bits xor_2_bits_8 (.A(A[1]), .B(B[1]), .S(S[1]));
endmodule

module somador_2_bits (
  input  A,
  input  B,
  input  Cin,
  output S,
  output Cout
);

  wire and_1_out, and_2_out, and_3_out, and_4_out, and_5_out, and_6_out, and_7_out, and_8_out, and_9_out,
       and_10_out, and_11_out, not_1_out, not_2_out, not_3_out, not_4_out, not_5_out, not_6_out, or_1_out,
       or_3_out, or_5_out;

  not not_1 (not_1_out, A);
  not not_2 (not_2_out, B);
  not not_3 (not_3_out, A);
  not not_4 (not_4_out, Cin);
  not not_5 (not_5_out, B);
  not not_6 (not_6_out, Cin);
  and and_1 (and_1_out, B, Cin);
  and and_2 (and_2_out, A, Cin);
  and and_3 (and_3_out, A, B);
  and and_4 (and_4_out, not_1_out, not_2_out);
  and and_5 (and_5_out, not_3_out, B);
  and and_6 (and_6_out, A, not_5_out);
  and and_7 (and_7_out, A, B);
  or or_1 (or_1_out, and_1_out, and_2_out);
  and and_8 (and_8_out, and_4_out, Cin);
  and and_9 (and_9_out, and_5_out, not_4_out);
  and and_10 (and_10_out, and_6_out, not_6_out);
  and and_11 (and_11_out, and_7_out, Cin);
  or or_2 (Cout, or_1_out, and_3_out);
  or or_3 (or_3_out, and_8_out, and_9_out);
  or or_4 (S, or_3_out, or_5_out);
  or or_5 (or_5_out, and_10_out, and_11_out);
endmodule

module somador_8_bits (
  input  Cin,
  input  [7:0] A,
  input  [7:0] B,
  output [7:0] S,
  output Cout
);

  wire somador_2_bits_2_cout, somador_2_bits_3_cout, somador_2_bits_4_cout, somador_2_bits_5_cout,
       somador_2_bits_6_cout, somador_2_bits_7_cout, somador_2_bits_8_cout;

  somador_2_bits somador_2_bits_1 (.A(A[7]), .B(B[7]), .Cin(somador_2_bits_2_cout), .S(S[7]), .Cout(Cout));
  somador_2_bits somador_2_bits_2 (
    .A(A[6]), .B(B[6]), .Cin(somador_2_bits_3_cout), .S(S[6]), .Cout(somador_2_bits_2_cout));
  somador_2_bits somador_2_bits_3 (
    .A(A[5]), .B(B[5]), .Cin(somador_2_bits_4_cout), .S(S[5]), .Cout(somador_2_bits_3_cout));
  somador_2_bits somador_2_bits_4 (
    .A(A[4]), .B(B[4]), .Cin(somador_2_bits_5_cout), .S(S[4]), .Cout(somador_2_bits_4_cout));
  somador_2_bits somador_2_bits_5 (
    .A(A[3]), .B(B[3]), .Cin(somador_2_bits_6_cout), .S(S[3]), .Cout(somador_2_bits_5_cout));
  somador_2_bits somador_2_bits_6 (
    .A(A[2]), .B(B[2]), .Cin(somador_2_bits_7_cout), .S(S[2]), .Cout(somador_2_bits_6_cout));
  somador_2_bits somador_2_bits_7 (
    .A(A[1]), .B(B[1]), .Cin(somador_2_bits_8_cout), .S(S[1]), .Cout(somador_2_bits_7_cout));
  somador_2_bits somador_2_bits_8 (.A(A[0]), .B(B[0]), .Cin(Cin), .S(S[0]), .Cout(somador_2_bits_8_cout));
endmodule

module Subtracao_8_bits (
  input  Cin,
  input  [7:0] A,
  input  [7:0] B,
  output [7:0] S,
  output Cout
);

  wire not_2_out, not_3_out, not_4_out, not_5_out, not_6_out, not_7_out, not_8_out, not_9_out, not_10_out,
       somador_2_bits_1_cout, somador_2_bits_2_cout, somador_2_bits_3_cout, somador_2_bits_4_cout,
       somador_2_bits_5_cout, somador_2_bits_6_cout, somador_2_bits_7_cout, somador_2_bits_8_cout;

  not not_1 (Cout, somador_2_bits_1_cout);
  somador_2_bits somador_2_bits_1 (
    .A(A[7]), .B(not_2_out), .Cin(somador_2_bits_2_cout), .S(S[7]), .Cout(somador_2_bits_1_cout));
  not not_2 (not_2_out, B[7]);
  not not_3 (not_3_out, B[6]);
  not not_4 (not_4_out, B[5]);
  not not_5 (not_5_out, B[4]);
  not not_6 (not_6_out, B[3]);
  not not_7 (not_7_out, B[2]);
  not not_8 (not_8_out, B[1]);
  not not_9 (not_9_out, B[0]);
  somador_2_bits somador_2_bits_2 (
    .A(A[6]), .B(not_3_out), .Cin(somador_2_bits_3_cout), .S(S[6]), .Cout(somador_2_bits_2_cout));
  somador_2_bits somador_2_bits_3 (
    .A(A[5]), .B(not_4_out), .Cin(somador_2_bits_4_cout), .S(S[5]), .Cout(somador_2_bits_3_cout));
  somador_2_bits somador_2_bits_4 (
    .A(A[4]), .B(not_5_out), .Cin(somador_2_bits_5_cout), .S(S[4]), .Cout(somador_2_bits_4_cout));
  somador_2_bits somador_2_bits_5 (
    .A(A[3]), .B(not_6_out), .Cin(somador_2_bits_6_cout), .S(S[3]), .Cout(somador_2_bits_5_cout));
  somador_2_bits somador_2_bits_6 (
    .A(A[2]), .B(not_7_out), .Cin(somador_2_bits_7_cout), .S(S[2]), .Cout(somador_2_bits_6_cout));
  somador_2_bits somador_2_bits_7 (
    .A(A[1]), .B(not_8_out), .Cin(somador_2_bits_8_cout), .S(S[1]), .Cout(somador_2_bits_7_cout));
  somador_2_bits somador_2_bits_8 (.A(A[0]), .B(not_9_out), .Cin(not_10_out), .S(S[0]), .Cout(somador_2_bits_8_cout));
  not not_10 (not_10_out, Cin);
endmodule

module Shift_Left_8_bits (
  input  Cin,
  input  [7:0] B,
  output [7:0] S,
  output Cout
);


  assign Cout = B[7];
  assign S = {B[6:0], Cin};
endmodule

module Shift_Right_8_bits (
  input  [7:0] B,
  input  Cin,
  output Cout,
  output [7:0] S
);


  assign Cout = B[0];
  assign S = {Cin, B[7:1]};
endmodule

module Decodificador_4_b (
  input  a0,
  input  a1,
  input  a2,
  input  a3,
  output a,
  output b,
  output c,
  output d,
  output e,
  output f,
  output g
);

  wire and_1_out, and_2_out, and_3_out, and_4_out, and_5_out, and_6_out, and_7_out, and_8_out, and_9_out,
       and_10_out, and_11_out, and_12_out, and_13_out, and_14_out, and_15_out, and_16_out, and_17_out,
       and_18_out, and_19_out, and_20_out, and_21_out, and_22_out, and_23_out, and_24_out, and_25_out,
       and_26_out, and_27_out, and_28_out, and_29_out, and_30_out, and_31_out, and_32_out, and_33_out,
       and_34_out, and_35_out, and_36_out, and_37_out, and_38_out, and_39_out, and_40_out, and_41_out,
       and_42_out, and_43_out, and_44_out, and_45_out, and_46_out, and_47_out, not_1_out, not_2_out,
       not_3_out, not_4_out, not_5_out, not_6_out, not_7_out, not_8_out, not_9_out, not_10_out, not_11_out,
       not_12_out, not_13_out, not_14_out, not_15_out, not_16_out, not_17_out, not_18_out, not_19_out,
       not_20_out, not_21_out, not_22_out, not_23_out, not_24_out, not_25_out, not_26_out, not_27_out,
       not_28_out, not_29_out, not_30_out, not_31_out, not_32_out, not_33_out, not_34_out, not_35_out,
       not_36_out, not_37_out, not_38_out, not_39_out, not_40_out, not_41_out, not_42_out, not_43_out,
       not_44_out, or_1_out, or_2_out, or_3_out, or_4_out, or_5_out, or_6_out, or_7_out, or_8_out, or_9_out,
       or_10_out, or_12_out, or_13_out, or_14_out, or_15_out, or_16_out, or_17_out, or_18_out, or_20_out,
       or_21_out, or_22_out, or_23_out;

  not not_1 (not_1_out, a1);
  not not_2 (not_2_out, a3);
  not not_3 (not_3_out, a0);
  not not_4 (not_4_out, a0);
  and and_1 (and_1_out, a0, not_5_out);
  not not_5 (not_5_out, a1);
  not not_6 (not_6_out, a2);
  not not_7 (not_7_out, a0);
  not not_8 (not_8_out, a1);
  not not_9 (not_9_out, a0);
  and and_2 (and_2_out, not_9_out, not_10_out);
  not not_10 (not_10_out, a2);
  not not_11 (not_11_out, a3);
  not not_12 (not_12_out, a0);
  not not_13 (not_13_out, a2);
  not not_14 (not_14_out, a0);
  and and_3 (and_3_out, not_14_out, not_15_out);
  not not_15 (not_15_out, a2);
  not not_16 (not_16_out, a0);
  and and_4 (and_4_out, not_16_out, a3);
  not not_17 (not_17_out, a2);
  not not_18 (not_18_out, a0);
  not not_19 (not_19_out, a1);
  not not_20 (not_20_out, a0);
  and and_5 (and_5_out, not_20_out, not_21_out);
  not not_21 (not_21_out, a1);
  not not_22 (not_22_out, a3);
  not not_23 (not_23_out, a1);
  and and_6 (and_6_out, not_23_out, a2);
  not not_24 (not_24_out, a2);
  not not_25 (not_25_out, a2);
  not not_26 (not_26_out, a1);
  and and_7 (and_7_out, not_26_out, not_27_out);
  not not_27 (not_27_out, a3);
  and and_8 (and_8_out, a2, not_28_out);
  not not_28 (not_28_out, a3);
  and and_9 (and_9_out, a0, a2);
  and and_10 (and_10_out, a0, a1);
  not not_29 (not_29_out, a2);
  not not_30 (not_30_out, a3);
  not not_31 (not_31_out, a0);
  and and_11 (and_11_out, not_31_out, a1);
  not not_32 (not_32_out, a2);
  not not_33 (not_33_out, a1);
  and and_12 (and_12_out, not_33_out, a2);
  and and_13 (and_13_out, a2, not_34_out);
  not not_34 (not_34_out, a3);
  not not_35 (not_35_out, a0);
  and and_14 (and_14_out, not_35_out, a1);
  not not_36 (not_36_out, a2);
  not not_37 (not_37_out, a1);
  and and_15 (and_15_out, not_1_out, not_2_out);
  and and_16 (and_16_out, not_3_out, a2);
  and and_17 (and_17_out, not_4_out, a1);
  and and_18 (and_18_out, a1, a2);
  and and_19 (and_19_out, and_1_out, not_6_out);
  not not_38 (not_38_out, a3);
  and and_20 (and_20_out, not_7_out, not_8_out);
  and and_21 (and_21_out, and_2_out, not_11_out);
  not not_39 (not_39_out, a1);
  not not_40 (not_40_out, a3);
  and and_22 (and_22_out, not_12_out, a2);
  and and_23 (and_23_out, a0, not_13_out);
  or or_1 (or_1_out, and_3_out, and_4_out);
  and and_24 (and_24_out, not_17_out, a3);
  and and_25 (and_25_out, not_18_out, a1);
  and and_26 (and_26_out, a0, not_19_out);
  and and_27 (and_27_out, and_5_out, not_22_out);
  and and_28 (and_28_out, and_6_out, a3);
  and and_29 (and_29_out, a1, not_24_out);
  and and_30 (and_30_out, a1, a2);
  not not_41 (not_41_out, a3);
  and and_31 (and_31_out, a0, not_25_out);
  not not_42 (not_42_out, a3);
  or or_2 (or_2_out, and_7_out, and_8_out);
  or or_3 (or_3_out, and_9_out, and_10_out);
  and and_32 (and_32_out, not_29_out, not_30_out);
  and and_33 (and_33_out, and_11_out, not_32_out);
  not not_43 (not_43_out, a3);
  not not_44 (not_44_out, a1);
  or or_4 (or_4_out, and_12_out, and_13_out);
  and and_34 (and_34_out, and_14_out, not_36_out);
  and and_35 (and_35_out, a0, not_37_out);
  and and_36 (and_36_out, a0, a3);
  or or_5 (or_5_out, and_15_out, and_16_out);
  and and_37 (and_37_out, and_17_out, a3);
  or or_6 (or_6_out, and_18_out, and_19_out);
  and and_38 (and_38_out, a0, not_38_out);
  or or_7 (or_7_out, and_20_out, and_21_out);
  and and_39 (and_39_out, not_39_out, not_40_out);
  and and_40 (and_40_out, and_22_out, a3);
  and and_41 (and_41_out, and_23_out, a3);
  or or_8 (or_8_out, or_1_out, and_24_out);
  or or_9 (or_9_out, and_25_out, and_26_out);
  or or_10 (or_10_out, and_27_out, and_28_out);
  and and_42 (and_42_out, and_29_out, a3);
  and and_43 (and_43_out, and_30_out, not_41_out);
  and and_44 (and_44_out, and_31_out, not_42_out);
  or or_11 (e, or_2_out, or_3_out);
  or or_12 (or_12_out, and_32_out, and_33_out);
  and and_45 (and_45_out, a1, not_43_out);
  and and_46 (and_46_out, a0, not_44_out);
  and and_47 (and_47_out, a0, a2);
  or or_13 (or_13_out, or_4_out, and_34_out);
  or or_14 (or_14_out, and_35_out, and_36_out);
  or or_15 (or_15_out, or_5_out, and_37_out);
  or or_16 (or_16_out, or_6_out, and_38_out);
  or or_17 (or_17_out, or_7_out, and_39_out);
  or or_18 (or_18_out, and_40_out, and_41_out);
  or or_19 (c, or_8_out, or_9_out);
  or or_20 (or_20_out, or_10_out, and_42_out);
  or or_21 (or_21_out, and_43_out, and_44_out);
  or or_22 (or_22_out, or_12_out, and_45_out);
  or or_23 (or_23_out, and_46_out, and_47_out);
  or or_24 (g, or_13_out, or_14_out);
  or or_25 (a, or_15_out, or_16_out);
  or or_26 (b, or_17_out, or_18_out);
  or or_27 (d, or_20_out, or_21_out);
  or or_28 (f, or_22_out, or_23_out);
endmodule

module Igual_0_8b (
  input  [7:0] a,
  output s
);

  wire or_1_out, or_2_out, or_3_out, or_4_out, or_5_out, or_6_out, or_7_out;

  or or_1 (or_1_out, or_2_out, or_6_out);
  or or_2 (or_2_out, a[7], a[6]);
  not not_1 (s, or_3_out);
  or or_3 (or_3_out, or_1_out, or_4_out);
  or or_4 (or_4_out, or_5_out, or_7_out);
  or or_5 (or_5_out, a[3], a[2]);
  or or_6 (or_6_out, a[5], a[4]);
  or or_7 (or_7_out, a[1], a[0]);
endmodule

module MUL_2_1_b (
  input  a,
  input  b,
  input  c,
  output s
);

  wire and_1_out, and_2_out, not_1_out;

  not not_1 (not_1_out, c);
  and and_1 (and_1_out, b, c);
  and and_2 (and_2_out, a, not_1_out);
  or or_1 (s, and_1_out, and_2_out);
endmodule

module MUL_2_1_8Bits_b (
  input  [7:0] A,
  input  [7:0] B,
  input  C,
  output [7:0] S
);

  MUL_2_1_b mul_2_1_b_1 (.a(B[0]), .b(A[0]), .c(C), .s(S[0]));
  MUL_2_1_b mul_2_1_b_2 (.a(B[1]), .b(A[1]), .c(C), .s(S[1]));
  MUL_2_1_b mul_2_1_b_3 (.a(B[2]), .b(A[2]), .c(C), .s(S[2]));
  MUL_2_1_b mul_2_1_b_4 (.a(B[3]), .b(A[3]), .c(C), .s(S[3]));
  MUL_2_1_b mul_2_1_b_5 (.a(B[4]), .b(A[4]), .c(C), .s(S[4]));
  MUL_2_1_b mul_2_1_b_6 (.a(B[5]), .b(A[5]), .c(C), .s(S[5]));
  MUL_2_1_b mul_2_1_b_7 (.a(B[6]), .b(A[6]), .c(C), .s(S[6]));
  MUL_2_1_b mul_2_1_b_8 (.a(B[7]), .b(A[7]), .c(C), .s(S[7]));
endmodule

module MUL_8_1_8bits (
  input  [2:0] OP,
  input  [7:0] XXX,
  input  [7:0] SHR,
  input  [7:0] SHL,
  input  [7:0] E,
  input  [7:0] OU,
  input  [7:0] CHOR,
  input  [7:0] SUB,
  input  [7:0] ADD,
  output [7:0] S
);

  wire [7:0] mul_2_1_8bits_b_1_s, mul_2_1_8bits_b_2_s, mul_2_1_8bits_b_3_s, mul_2_1_8bits_b_4_s,
       mul_2_1_8bits_b_5_s, mul_2_1_8bits_b_6_s;

  MUL_2_1_8Bits_b mul_2_1_8bits_b_1 (.A(XXX), .B(SHR), .S(mul_2_1_8bits_b_1_s), .C(OP[0]));
  MUL_2_1_8Bits_b mul_2_1_8bits_b_2 (.A(SHL), .B(E), .S(mul_2_1_8bits_b_2_s), .C(OP[0]));
  MUL_2_1_8Bits_b mul_2_1_8bits_b_3 (.A(OU), .B(CHOR), .S(mul_2_1_8bits_b_3_s), .C(OP[0]));
  MUL_2_1_8Bits_b mul_2_1_8bits_b_4 (.A(SUB), .B(ADD), .S(mul_2_1_8bits_b_4_s), .C(OP[0]));
  MUL_2_1_8Bits_b mul_2_1_8bits_b_5 (
    .A(mul_2_1_8bits_b_1_s), .B(mul_2_1_8bits_b_2_s), .S(mul_2_1_8bits_b_5_s), .C(OP[1]));
  MUL_2_1_8Bits_b mul_2_1_8bits_b_6 (
    .A(mul_2_1_8bits_b_3_s), .B(mul_2_1_8bits_b_4_s), .S(mul_2_1_8bits_b_6_s), .C(OP[1]));
  MUL_2_1_8Bits_b mul_2_1_8bits_b_7 (.A(mul_2_1_8bits_b_5_s), .B(mul_2_1_8bits_b_6_s), .S(S), .C(OP[2]));
endmodule

module Decodificador_Carry (
  input  SUB,
  input  ADD,
  input  SHL,
  input  SHR,
  input  [2:0] OP,
  output C
);

  wire mul_2_1_b_1_s, mul_2_1_b_2_s, mul_2_1_b_3_s, mul_2_1_b_4_s, mul_2_1_b_5_s;

  MUL_2_1_b mul_2_1_b_1 (.a(ADD), .b(SUB), .c(OP[0]), .s(mul_2_1_b_1_s));
  MUL_2_1_b mul_2_1_b_2 (.a(1'b0), .b(SHL), .c(OP[0]), .s(mul_2_1_b_2_s));
  MUL_2_1_b mul_2_1_b_3 (.a(SHR), .b(1'b0), .c(OP[0]), .s(mul_2_1_b_3_s));
  MUL_2_1_b mul_2_1_b_4 (.a(mul_2_1_b_1_s), .b(1'b0), .c(OP[1]), .s(mul_2_1_b_4_s));
  MUL_2_1_b mul_2_1_b_5 (.a(mul_2_1_b_2_s), .b(mul_2_1_b_3_s), .c(OP[1]), .s(mul_2_1_b_5_s));
  MUL_2_1_b mul_2_1_b_6 (.a(mul_2_1_b_4_s), .b(mul_2_1_b_5_s), .c(OP[2]), .s(C));
endmodule

module Decodificador_4b (
  input  [3:0] OP
);

  wire mul_16_1_1b_1_out_18, mul_16_1_1b_2_out_18, mul_16_1_1b_3_out_18, mul_16_1_1b_4_out_18,
       mul_16_1_1b_5_out_18, mul_16_1_1b_6_out_18, mul_16_1_1b_7_out_18, undriven, undriven_2, undriven_3,
       undriven_4, undriven_5, undriven_6, undriven_7;

  MUL_16_1_1b mul_16_1_1b_1 (
    .in_10(undriven), .in_11(undriven), .in_13(1'b0), .in_14(1'b1), .in_15(1'b1), .in_16(1'b1), .in_17(1'b1),
    .OP(OP), .out_18(mul_16_1_1b_1_out_18));  // open: in_2, in_3, in_4, in_5, in_6, in_7, in_8, in_9, in_12
  MUL_16_1_1b mul_16_1_1b_2 (
    .in_10(undriven_2), .in_11(undriven_2), .in_13(1'b1), .in_14(1'b1), .in_15(1'b0), .in_16(1'b1),
    .in_17(1'b1), .OP(OP), .out_18(mul_16_1_1b_2_out_18));  // open: in_2, in_3, in_4, in_5, in_6, in_7, in_8, in_9, in_12
  MUL_16_1_1b mul_16_1_1b_3 (
    .in_10(undriven_3), .in_11(undriven_3), .in_13(1'b1), .in_14(1'b1), .in_15(1'b1), .in_16(1'b0),
    .in_17(1'b1), .OP(OP), .out_18(mul_16_1_1b_3_out_18));  // open: in_2, in_3, in_4, in_5, in_6, in_7, in_8, in_9, in_12
  MUL_16_1_1b mul_16_1_1b_4 (
    .in_10(undriven_4), .in_11(undriven_4), .in_13(1'b0), .in_14(1'b0), .in_15(1'b1), .in_16(1'b0),
    .in_17(1'b1), .OP(OP), .out_18(mul_16_1_1b_4_out_18));  // open: in_2, in_3, in_4, in_5, in_6, in_7, in_8, in_9, in_12
  MUL_16_1_1b mul_16_1_1b_5 (
    .in_10(undriven_5), .in_11(undriven_5), .in_13(1'b1), .in_14(1'b0), .in_15(1'b0), .in_16(1'b0),
    .in_17(1'b1), .OP(OP), .out_18(mul_16_1_1b_5_out_18));  // open: in_2, in_3, in_4, in_5, in_6, in_7, in_8, in_9, in_12
  MUL_16_1_1b mul_16_1_1b_6 (
    .in_10(undriven_6), .in_11(undriven_6), .in_13(1'b1), .in_14(1'b1), .in_15(1'b1), .in_16(1'b0),
    .in_17(1'b1), .OP(OP), .out_18(mul_16_1_1b_6_out_18));  // open: in_2, in_3, in_4, in_5, in_6, in_7, in_8, in_9, in_12
  MUL_16_1_1b mul_16_1_1b_7 (
    .in_10(undriven_7), .in_11(undriven_7), .in_13(1'b1), .in_14(1'b1), .in_15(1'b1), .in_16(1'b0),
    .in_17(1'b0), .OP(OP), .out_18(mul_16_1_1b_7_out_18));  // open: in_2, in_3, in_4, in_5, in_6, in_7, in_8, in_9, in_12
  _7_Segment_Display u_7_segment_display_1 (
    .g(mul_16_1_1b_7_out_18), .f(mul_16_1_1b_5_out_18), .a(mul_16_1_1b_6_out_18), .b(mul_16_1_1b_1_out_18),
    .e(mul_16_1_1b_4_out_18), .d(mul_16_1_1b_3_out_18), .c(mul_16_1_1b_2_out_18));  // open: dp
endmodule

module MUL_16_1_1b (
  input  [3:0] OP,
  input  in_2,
  input  in_3,
  input  in_4,
  input  in_5,
  input  in_6,
  input  in_7,
  input  in_8,
  input  in_9,
  input  in_10,
  input  in_11,
  input  in_12,
  input  in_13,
  input  in_14,
  input  in_15,
  input  in_16,
  input  in_17,
  output out_18
);

  wire mul_2_1_b_1_s, mul_2_1_b_2_s, mul_2_1_b_3_s, mul_2_1_b_4_s, mul_2_1_b_5_s, mul_2_1_b_6_s,
       mul_2_1_b_7_s, mul_2_1_b_8_s, mul_2_1_b_9_s, mul_2_1_b_10_s, mul_2_1_b_11_s, mul_2_1_b_12_s,
       mul_2_1_b_13_s, mul_2_1_b_14_s;

  MUL_2_1_b mul_2_1_b_1 (.a(in_17), .b(in_16), .c(OP[0]), .s(mul_2_1_b_1_s));
  MUL_2_1_b mul_2_1_b_2 (.a(in_15), .b(in_14), .c(OP[0]), .s(mul_2_1_b_2_s));
  MUL_2_1_b mul_2_1_b_3 (.a(in_13), .b(in_12), .c(OP[0]), .s(mul_2_1_b_3_s));
  MUL_2_1_b mul_2_1_b_4 (.a(in_11), .b(in_10), .c(OP[0]), .s(mul_2_1_b_4_s));
  MUL_2_1_b mul_2_1_b_5 (.a(in_9), .b(in_8), .c(OP[0]), .s(mul_2_1_b_5_s));
  MUL_2_1_b mul_2_1_b_6 (.a(in_7), .b(in_6), .c(OP[0]), .s(mul_2_1_b_6_s));
  MUL_2_1_b mul_2_1_b_7 (.a(in_5), .b(in_4), .c(OP[0]), .s(mul_2_1_b_7_s));
  MUL_2_1_b mul_2_1_b_8 (.a(in_2), .b(in_2), .c(OP[0]), .s(mul_2_1_b_8_s));
  MUL_2_1_b mul_2_1_b_9 (.a(mul_2_1_b_1_s), .b(mul_2_1_b_2_s), .c(OP[1]), .s(mul_2_1_b_9_s));
  MUL_2_1_b mul_2_1_b_10 (.a(mul_2_1_b_3_s), .b(mul_2_1_b_4_s), .c(OP[1]), .s(mul_2_1_b_10_s));
  MUL_2_1_b mul_2_1_b_11 (.a(mul_2_1_b_5_s), .b(mul_2_1_b_6_s), .c(OP[1]), .s(mul_2_1_b_11_s));
  MUL_2_1_b mul_2_1_b_12 (.a(mul_2_1_b_7_s), .b(mul_2_1_b_8_s), .c(OP[1]), .s(mul_2_1_b_12_s));
  MUL_2_1_b mul_2_1_b_13 (.a(mul_2_1_b_9_s), .b(mul_2_1_b_10_s), .c(OP[2]), .s(mul_2_1_b_13_s));
  MUL_2_1_b mul_2_1_b_14 (.a(mul_2_1_b_11_s), .b(mul_2_1_b_12_s), .c(OP[2]), .s(mul_2_1_b_14_s));
  MUL_2_1_b mul_2_1_b_15 (.a(mul_2_1_b_13_s), .b(mul_2_1_b_14_s), .c(OP[3]), .s(out_18));
endmodule
