// Logisim project eld201802trab1.circ as structural Verilog: 2 circuits, main circuit main
module main (
);


  // Notes on the sheet:
  //   e depois use aquele circuito para construir sua calculadora.
  //   Este projeto foi fornecido apenas para que você altere o circuito alu-8-bits,
endmodule

module alu_8_bits (
  input  [7:0] A,
  input  [7:0] B,
  input  [2:0] OP,
  input  Cin,
  output [7:0] s,
  output c,
  output z
);
endmodule
