// Logisim project renan_trabalho.circ as structural Verilog: 24 circuits, main circuit Calculadora
module ADD (
  input  a,
  input  b,
  input  cin,
  output cout,
  output s
);

  wire and_1_out, and_2_out, and_3_out, and_4_out, and_5_out, and_6_out, and_7_out, not_1_out, not_2_out,
       not_3_out, not_4_out, not_5_out, not_6_out;

  and and_1 (and_1_out, b, cin);
  and and_2 (and_2_out, a, cin);
  and and_3 (and_3_out, a, b);
  not not_1 (not_1_out, a);
  not not_2 (not_2_out, b);
  not not_3 (not_3_out, a);
  not not_4 (not_4_out, cin);
  not not_5 (not_5_out, b);
  not not_6 (not_6_out, cin);
  or or_1 (cout, and_1_out, and_2_out, and_3_out);
  and and_4 (and_4_out, not_1_out, not_2_out, cin);
  and and_5 (and_5_out, not_3_out, b, not_4_out);
  and and_6 (and_6_out, a, not_5_out, not_6_out);
  and and_7 (and_7_out, a, b, cin);
  or or_2 (s, and_4_out, and_5_out, and_6_out, and_7_out);
endmodule

module Calculadora (
  input  in_1,
  input  [7:0] A,
  input  [7:0] B,
  input  [2:0] OP,
  output out_5
);

  wire [6:0] l_2_dec_16_fc21d418_1_out_2, l_2_dec_16_fc21d418_1_out_3;
  wire [7:0] alu_1_s;

  ALU alu_1 (.Cin(in_1), .A(A), .B(B), .OP(OP), .S(alu_1_s));  // open: Overflow_Borrow_75404fa1, z
  L_2_DEC_16_fc21d418 l_2_dec_16_fc21d418_1 (
    .Input(alu_1_s), .out_2(l_2_dec_16_fc21d418_1_out_2), .out_3(l_2_dec_16_fc21d418_1_out_3));
  _7_Segment_Display u_7_segment_display_1 (
    .g(l_2_dec_16_fc21d418_1_out_3[6]), .f(l_2_dec_16_fc21d418_1_out_3[5]),
    .a(l_2_dec_16_fc21d418_1_out_3[0]), .b(l_2_dec_16_fc21d418_1_out_3[1]),
    .e(l_2_dec_16_fc21d418_1_out_3[4]), .d(l_2_dec_16_fc21d418_1_out_3[3]), .c(l_2_dec_16_fc21d418_1_out_3[2]));  // open: dp
  _7_Segment_Display u_7_segment_display_2 (
    .g(l_2_dec_16_fc21d418_1_out_2[6]), .f(l_2_dec_16_fc21d418_1_out_2[5]),
    .a(l_2_dec_16_fc21d418_1_out_2[0]), .b(l_2_dec_16_fc21d418_1_out_2[1]),
    .e(l_2_dec_16_fc21d418_1_out_2[4]), .d(l_2_dec_16_fc21d418_1_out_2[3]), .c(l_2_dec_16_fc21d418_1_out_2[2]));  // open: dp
endmodule

module ADD_8 (
  input  [7:0] B,
  input  [7:0] A,
  input  Cin,
  output [7:0] S,
  output Cout
);

  wire add_1_cout, add_2_cout, add_3_cout, add_4_cout, add_5_cout, add_6_cout, add_7_cout;

  ADD add_1 (.a(A[0]), .b(B[0]), .cin(Cin), .cout(add_1_cout), .s(S[0]));
  ADD add_2 (.a(A[1]), .b(B[1]), .cin(add_1_cout), .cout(add_2_cout), .s(S[1]));
  ADD add_3 (.a(A[2]), .b(B[2]), .cin(add_2_cout), .cout(add_3_cout), .s(S[2]));
  ADD add_4 (.a(A[3]), .b(B[3]), .cin(add_3_cout), .cout(add_4_cout), .s(S[3]));
  ADD add_5 (.a(A[4]), .b(B[4]), .cin(add_4_cout), .cout(add_5_cout), .s(S[4]));
  ADD add_6 (.a(A[5]), .b(B[5]), .cin(add_5_cout), .cout(add_6_cout), .s(S[5]));
  ADD add_7 (.a(A[6]), .b(B[6]), .cin(add_6_cout), .cout(add_7_cout), .s(S[6]));
  ADD add_8 (.a(A[7]), .b(B[7]), .cin(add_7_cout), .cout(Cout), .s(S[7]));
endmodule

module XOR (
  input  a,
  input  b,
  output s
);

  wire and_1_out, and_2_out, not_1_out, not_2_out;

  not not_1 (not_1_out, a);
  not not_2 (not_2_out, b);
  and and_1 (and_1_out, not_1_out, b);
  and and_2 (and_2_out, a, not_2_out);
  or or_1 (s, and_1_out, and_2_out);
endmodule

module XOR_8 (
  input  [7:0] B,
  input  [7:0] A,
  output [7:0] out_3
);

  XOR xor_1 (.a(A[0]), .b(B[0]), .s(out_3[0]));
  XOR xor_2 (.a(A[1]), .b(B[1]), .s(out_3[1]));
  XOR xor_3 (.a(A[2]), .b(B[2]), .s(out_3[2]));
  XOR xor_4 (.a(A[3]), .b(B[3]), .s(out_3[3]));
  XOR xor_5 (.a(A[4]), .b(B[4]), .s(out_3[4]));
  XOR xor_6 (.a(A[5]), .b(B[5]), .s(out_3[5]));
  XOR xor_7 (.a(A[6]), .b(B[6]), .s(out_3[6]));
  XOR xor_8 (.a(A[7]), .b(B[7]), .s(out_3[7]));
endmodule

module OR (
  input  a,
  input  b,
  output s
);

  or or_1 (s, b, a);
endmodule

module OR_8 (
  input  [7:0] B,
  input  [7:0] A,
  output [7:0] out_3
);

  OR or_1 (.a(A[0]), .b(B[0]), .s(out_3[0]));
  OR or_2 (.a(A[1]), .b(B[1]), .s(out_3[1]));
  OR or_3 (.a(A[2]), .b(B[2]), .s(out_3[2]));
  OR or_4 (.a(A[3]), .b(B[3]), .s(out_3[3]));
  OR or_5 (.a(A[4]), .b(B[4]), .s(out_3[4]));
  OR or_6 (.a(A[5]), .b(B[5]), .s(out_3[5]));
  OR or_7 (.a(A[6]), .b(B[6]), .s(out_3[6]));
  OR or_8 (.a(A[7]), .b(B[7]), .s(out_3[7]));
endmodule

module AND (
  input  a,
  input  b,
  output s
);

  and and_1 (s, a, b);
endmodule

module AND_8 (
  input  [7:0] B,
  input  [7:0] A,
  output [7:0] out_3
);

  AND and_1 (.a(A[0]), .b(B[0]), .s(out_3[0]));
  AND and_2 (.a(A[1]), .b(B[1]), .s(out_3[1]));
  AND and_3 (.a(A[2]), .b(B[2]), .s(out_3[2]));
  AND and_4 (.a(A[3]), .b(B[3]), .s(out_3[3]));
  AND and_5 (.a(A[4]), .b(B[4]), .s(out_3[4]));
  AND and_6 (.a(A[5]), .b(B[5]), .s(out_3[5]));
  AND and_7 (.a(A[6]), .b(B[6]), .s(out_3[6]));
  AND and_8 (.a(A[7]), .b(B[7]), .s(out_3[7]));
endmodule

module DECODIFICADOR_16 (
  input  a0,
  input  a1,
  input  a2,
  input  a3,
  output a,
  output b,
  output c,
  output d,
  output e,
  output f,
  output g
);

  wire and_1_out, and_2_out, and_3_out, and_4_out, and_5_out, and_6_out, and_7_out, and_8_out, and_9_out,
       and_10_out, and_11_out, and_12_out, and_13_out, and_14_out, and_15_out, and_16_out, and_17_out,
       and_18_out, and_19_out, and_20_out, and_21_out, and_22_out, and_23_out, and_24_out, and_25_out,
       and_26_out, and_27_out, and_28_out, and_29_out, and_30_out, and_31_out, and_32_out, and_33_out,
       and_34_out, and_35_out, not_1_out, not_2_out, not_3_out, not_4_out, not_5_out, not_6_out, not_7_out,
       not_8_out, not_9_out, not_10_out, not_11_out, not_12_out, not_13_out, not_14_out, not_15_out,
       not_16_out, not_17_out, not_18_out, not_19_out, not_20_out, not_21_out, not_22_out, not_23_out,
       not_24_out, not_25_out, not_26_out, not_27_out, not_28_out, not_29_out, not_30_out, not_31_out,
       not_32_out, not_33_out, not_34_out, not_35_out, not_36_out, not_37_out, not_38_out, not_39_out,
       not_40_out, not_41_out, not_42_out, not_43_out, not_44_out;

  not not_1 (not_1_out, a1);
  and and_1 (and_1_out, not_1_out, not_2_out);
  not not_2 (not_2_out, a3);
  not not_3 (not_3_out, a0);
  and and_2 (and_2_out, not_3_out, a2);
  not not_4 (not_4_out, a0);
  and and_3 (and_3_out, not_4_out, a1, a3);
  and and_4 (and_4_out, a1, a2);
  and and_5 (and_5_out, a0, not_5_out, not_6_out);
  not not_5 (not_5_out, a1);
  not not_6 (not_6_out, a2);
  and and_6 (and_6_out, a0, not_7_out);
  not not_7 (not_7_out, a3);
  not not_8 (not_8_out, a0);
  and and_7 (and_7_out, not_8_out, not_9_out);
  not not_9 (not_9_out, a1);
  not not_10 (not_10_out, a0);
  and and_8 (and_8_out, not_10_out, not_11_out, not_12_out);
  not not_11 (not_11_out, a2);
  not not_12 (not_12_out, a3);
  not not_13 (not_13_out, a1);
  and and_9 (and_9_out, not_13_out, not_14_out);
  not not_14 (not_14_out, a3);
  not not_15 (not_15_out, a0);
  and and_10 (and_10_out, not_15_out, a2, a3);
  and and_11 (and_11_out, a0, not_16_out, a3);
  not not_16 (not_16_out, a2);
  not not_17 (not_17_out, a0);
  and and_12 (and_12_out, not_17_out, not_18_out);
  not not_18 (not_18_out, a2);
  not not_19 (not_19_out, a0);
  and and_13 (and_13_out, not_19_out, a3);
  not not_20 (not_20_out, a2);
  and and_14 (and_14_out, not_20_out, a3);
  not not_21 (not_21_out, a0);
  and and_15 (and_15_out, not_21_out, a1);
  and and_16 (and_16_out, a0, not_22_out);
  not not_22 (not_22_out, a1);
  not not_23 (not_23_out, a0);
  and and_17 (and_17_out, not_23_out, not_24_out, not_25_out);
  not not_24 (not_24_out, a1);
  not not_25 (not_25_out, a3);
  not not_26 (not_26_out, a1);
  and and_18 (and_18_out, not_26_out, a2, a3);
  not not_27 (not_27_out, a2);
  and and_19 (and_19_out, a1, not_27_out, a3);
  and and_20 (and_20_out, a1, a2, not_28_out);
  not not_28 (not_28_out, a3);
  not not_29 (not_29_out, a2);
  and and_21 (and_21_out, a0, not_29_out, not_30_out);
  not not_30 (not_30_out, a3);
  not not_31 (not_31_out, a1);
  and and_22 (and_22_out, not_31_out, not_32_out);
  not not_32 (not_32_out, a3);
  and and_23 (and_23_out, a2, not_33_out);
  not not_33 (not_33_out, a3);
  and and_24 (and_24_out, a0, a2);
  and and_25 (and_25_out, a0, a1);
  not not_34 (not_34_out, a2);
  and and_26 (and_26_out, not_34_out, not_35_out);
  not not_35 (not_35_out, a3);
  not not_36 (not_36_out, a0);
  and and_27 (and_27_out, not_36_out, a1, not_37_out);
  not not_37 (not_37_out, a2);
  and and_28 (and_28_out, a1, not_38_out);
  not not_38 (not_38_out, a3);
  and and_29 (and_29_out, a0, not_39_out);
  not not_39 (not_39_out, a1);
  and and_30 (and_30_out, a0, a2);
  not not_40 (not_40_out, a1);
  and and_31 (and_31_out, not_40_out, a2);
  and and_32 (and_32_out, a2, not_41_out);
  not not_41 (not_41_out, a3);
  not not_42 (not_42_out, a0);
  and and_33 (and_33_out, not_42_out, a1, not_43_out);
  not not_43 (not_43_out, a2);
  and and_34 (and_34_out, a0, not_44_out);
  not not_44 (not_44_out, a1);
  and and_35 (and_35_out, a0, a3);
  or or_1 (b, and_7_out, and_8_out, and_10_out, and_11_out);
  or or_2 (d, and_17_out, and_18_out, and_20_out, and_21_out);
  or or_3 (e, and_22_out, and_23_out, and_24_out, and_25_out);
  or or_4 (f, and_26_out, and_27_out, and_28_out, and_29_out, and_30_out);
  or or_5 (g, and_31_out, and_32_out, and_33_out, and_34_out, and_35_out);
  or or_6 (a, and_1_out, and_2_out, and_3_out, and_4_out, and_5_out, and_6_out);
  or or_7 (c, and_12_out, and_13_out, and_15_out, and_16_out);
endmodule

module L_2_DEC_16_fc21d418 (
  input  [7:0] Input,
  output [6:0] out_2,
  output [6:0] out_3
);

  DECODIFICADOR_16 decodificador_16_1 (
    .a0(Input[7]), .a1(Input[6]), .a2(Input[5]), .a3(Input[4]), .a(out_2[0]), .b(out_2[1]), .c(out_2[2]),
    .d(out_2[3]), .e(out_2[4]), .f(out_2[5]), .g(out_2[6]));
  DECODIFICADOR_16 decodificador_16_2 (
    .a0(Input[3]), .a1(Input[2]), .a2(Input[1]), .a3(Input[0]), .a(out_3[0]), .b(out_3[1]), .c(out_3[2]),
    .d(out_3[3]), .e(out_3[4]), .f(out_3[5]), .g(out_3[6]));
endmodule

module SUB_8 (
  input  [7:0] B,
  input  [7:0] A,
  output [7:0] S,
  output Borrow
);

  wire add_1_cout, add_2_cout, add_3_cout, add_4_cout, add_5_cout, add_6_cout, add_7_cout, not_1_out,
       not_2_out, not_3_out, not_4_out, not_5_out, not_6_out, not_7_out, not_8_out;

  not not_1 (not_1_out, B[0]);
  not not_2 (not_2_out, B[1]);
  not not_3 (not_3_out, B[2]);
  not not_4 (not_4_out, B[3]);
  not not_5 (not_5_out, B[4]);
  not not_6 (not_6_out, B[5]);
  not not_7 (not_7_out, B[6]);
  not not_8 (not_8_out, B[7]);
  ADD add_1 (.a(A[0]), .b(not_1_out), .cin(1'b1), .cout(add_1_cout), .s(S[0]));
  ADD add_2 (.a(A[1]), .b(not_2_out), .cin(add_1_cout), .cout(add_2_cout), .s(S[1]));
  ADD add_3 (.a(A[2]), .b(not_3_out), .cin(add_2_cout), .cout(add_3_cout), .s(S[2]));
  ADD add_4 (.a(A[3]), .b(not_4_out), .cin(add_3_cout), .cout(add_4_cout), .s(S[3]));
  ADD add_5 (.a(A[4]), .b(not_5_out), .cin(add_4_cout), .cout(add_5_cout), .s(S[4]));
  ADD add_6 (.a(A[5]), .b(not_6_out), .cin(add_5_cout), .cout(add_6_cout), .s(S[5]));
  ADD add_7 (.a(A[6]), .b(not_7_out), .cin(add_6_cout), .cout(add_7_cout), .s(S[6]));
  ADD add_8 (.a(A[7]), .b(not_8_out), .cin(add_7_cout), .cout(Borrow), .s(S[7]));
endmodule

module SHL (
  input  [7:0] in_1,
  output [7:0] out_2,
  output out_3
);


  assign out_2 = {in_1[6:0], 1'b0};
  assign out_3 = in_1[7];
endmodule

module SHR (
  input  [7:0] in_1,
  output out_2,
  output [7:0] out_3
);


  assign out_2 = in_1[0];
  assign out_3 = {1'b0, in_1[7:1]};
endmodule

module MUL_2_1_b (
  input  a,
  input  b,
  input  c,
  output s
);

  wire and_1_out, and_2_out, not_1_out;

  not not_1 (not_1_out, c);
  and and_1 (and_1_out, b, c);
  and and_2 (and_2_out, a, not_1_out);
  or or_1 (s, and_1_out, and_2_out);
endmodule

module MUL_2_1_8Bits_b (
  input  [7:0] in_1,
  input  [7:0] in_2,
  input  in_3,
  output [7:0] out_4
);

  MUL_2_1_b mul_2_1_b_1 (.a(in_2[0]), .b(in_1[0]), .c(in_3), .s(out_4[0]));
  MUL_2_1_b mul_2_1_b_2 (.a(in_2[1]), .b(in_1[1]), .c(in_3), .s(out_4[1]));
  MUL_2_1_b mul_2_1_b_3 (.a(in_2[2]), .b(in_1[2]), .c(in_3), .s(out_4[2]));
  MUL_2_1_b mul_2_1_b_4 (.a(in_2[3]), .b(in_1[3]), .c(in_3), .s(out_4[3]));
  MUL_2_1_b mul_2_1_b_5 (.a(in_2[4]), .b(in_1[4]), .c(in_3), .s(out_4[4]));
  MUL_2_1_b mul_2_1_b_6 (.a(in_2[5]), .b(in_1[5]), .c(in_3), .s(out_4[5]));
  MUL_2_1_b mul_2_1_b_7 (.a(in_2[6]), .b(in_1[6]), .c(in_3), .s(out_4[6]));
  MUL_2_1_b mul_2_1_b_8 (.a(in_2[7]), .b(in_1[7]), .c(in_3), .s(out_4[7]));
endmodule

module MUL_8_1_8Bits_8 (
  input  [7:0] NONE,
  input  [7:0] OR,
  input  [7:0] SHIFT_LEFT,
  input  [7:0] SUBTRACAO,
  input  [7:0] SHIFT_RIGHT,
  input  [7:0] XOR,
  input  [7:0] AND,
  input  [7:0] SOMA,
  input  [2:0] in_9,
  output [7:0] out_10
);

  wire [7:0] mul_2_1_8bits_b_1_out_4, mul_2_1_8bits_b_2_out_4, mul_2_1_8bits_b_3_out_4,
       mul_2_1_8bits_b_4_out_4, mul_2_1_8bits_b_5_out_4, mul_2_1_8bits_b_6_out_4;

  MUL_2_1_8Bits_b mul_2_1_8bits_b_1 (.in_1(NONE), .in_2(OR), .in_3(in_9[2]), .out_4(mul_2_1_8bits_b_1_out_4));
  MUL_2_1_8Bits_b mul_2_1_8bits_b_2 (
    .in_1(SHIFT_LEFT), .in_2(SUBTRACAO), .in_3(in_9[2]), .out_4(mul_2_1_8bits_b_2_out_4));
  MUL_2_1_8Bits_b mul_2_1_8bits_b_3 (.in_1(SHIFT_RIGHT), .in_2(XOR), .in_3(in_9[2]), .out_4(mul_2_1_8bits_b_3_out_4));
  MUL_2_1_8Bits_b mul_2_1_8bits_b_4 (.in_1(AND), .in_2(SOMA), .in_3(in_9[2]), .out_4(mul_2_1_8bits_b_4_out_4));
  MUL_2_1_8Bits_b mul_2_1_8bits_b_5 (
    .in_1(mul_2_1_8bits_b_1_out_4), .in_2(mul_2_1_8bits_b_2_out_4), .in_3(in_9[1]),
    .out_4(mul_2_1_8bits_b_5_out_4));
  MUL_2_1_8Bits_b mul_2_1_8bits_b_6 (
    .in_1(mul_2_1_8bits_b_3_out_4), .in_2(mul_2_1_8bits_b_4_out_4), .in_3(in_9[1]),
    .out_4(mul_2_1_8bits_b_6_out_4));
  MUL_2_1_8Bits_b mul_2_1_8bits_b_7 (
    .in_1(mul_2_1_8bits_b_5_out_4), .in_2(mul_2_1_8bits_b_6_out_4), .in_3(in_9[0]), .out_4(out_10));
endmodule

module ALU (
  input  Cin,
  input  [7:0] A,
  input  [7:0] B,
  input  [2:0] OP,
  output [7:0] S,
  output z,
  output Overflow_Borrow_75404fa1
);

  wire add_8_1_cout, shl_1_out_3, shr_1_out_2, sub_8_1_borrow;
  wire [7:0] add_8_1_s, and_8_1_out_3, or_8_1_out_3, shl_1_out_2, shr_1_out_3, sub_8_1_s, xor_8_1_out_3;

  SHL shl_1 (.in_1(A), .out_2(shl_1_out_2), .out_3(shl_1_out_3));
  SUB_8 sub_8_1 (.B(B), .A(A), .S(sub_8_1_s), .Borrow(sub_8_1_borrow));
  SHR shr_1 (.in_1(A), .out_3(shr_1_out_3), .out_2(shr_1_out_2));
  XOR_8 xor_8_1 (.B(B), .A(A), .out_3(xor_8_1_out_3));
  AND_8 and_8_1 (.B(B), .A(A), .out_3(and_8_1_out_3));
  MUL_Overflow mul_overflow_1 (
    .a(add_8_1_cout), .b(sub_8_1_borrow), .c(shl_1_out_3), .d(shr_1_out_2), .OP(OP),
    .out_6(Overflow_Borrow_75404fa1));
  OR_8 or_8_1 (.B(B), .A(A), .out_3(or_8_1_out_3));
  MUL_8_1_8Bits_8 mul_8_1_8bits_8_1 (
    .NONE({8{1'b0}}), .OR(or_8_1_out_3), .SHIFT_LEFT(shl_1_out_2), .SUBTRACAO(sub_8_1_s),
    .SHIFT_RIGHT(shr_1_out_3), .XOR(xor_8_1_out_3), .AND(and_8_1_out_3), .SOMA(add_8_1_s), .in_9(OP),
    .out_10(S));
  ADD_8 add_8_1 (.B(B), .A(A), .S(add_8_1_s), .Cout(add_8_1_cout), .Cin(Cin));
  COMP_8 comp_8_1 (.A(S), .out_2(z));
endmodule

module ALU_16 (
  input  Cin,
  input  [2:0] OP,
  input  [15:0] A,
  input  [15:0] B,
  output out_5,
  output [15:0] out_6,
  output z
);

  wire alu_1_overflow_borrow_75404fa1, alu_1_z, alu_2_z, or_1_s;

  OR or_1 (.a(z), .b(Cin), .s(or_1_s));
  ALU alu_1 (
    .Cin(or_1_s), .A(A[7:0]), .B(B[7:0]), .OP(OP), .S(out_6[7:0]),
    .Overflow_Borrow_75404fa1(alu_1_overflow_borrow_75404fa1), .z(alu_1_z));
  ALU alu_2 (
    .Cin(alu_1_overflow_borrow_75404fa1), .A(A[15:8]), .B(B[15:8]), .OP(OP), .S(out_6[15:8]),
    .Overflow_Borrow_75404fa1(out_5), .z(alu_2_z));
  and and_1 (z, alu_1_z, alu_2_z);
endmodule

module COMP (
  input  a,
  input  b,
  output c
);

  wire not_1_out, not_2_out;

  not not_1 (not_1_out, a);
  not not_2 (not_2_out, b);
  and and_1 (c, not_1_out, not_2_out);
endmodule

module COMP_8 (
  input  [7:0] A,
  output out_2
);

  wire and_1_out, and_2_out, and_3_out, and_4_out, and_5_out, and_6_out, comp_1_c, comp_2_c, comp_3_c,
       comp_4_c, comp_5_c, comp_6_c, comp_7_c, comp_8_c;

  COMP comp_1 (.a(A[0]), .b(1'b0), .c(comp_1_c));
  COMP comp_2 (.a(A[1]), .b(1'b0), .c(comp_2_c));
  COMP comp_3 (.a(A[2]), .b(1'b0), .c(comp_3_c));
  COMP comp_4 (.a(A[3]), .b(1'b0), .c(comp_4_c));
  COMP comp_5 (.a(A[4]), .b(1'b0), .c(comp_5_c));
  COMP comp_6 (.a(A[5]), .b(1'b0), .c(comp_6_c));
  COMP comp_7 (.a(A[6]), .b(1'b0), .c(comp_7_c));
  COMP comp_8 (.a(A[7]), .b(1'b0), .c(comp_8_c));
  and and_1 (and_1_out, comp_1_c, comp_2_c);
  and and_2 (and_2_out, comp_3_c, comp_4_c);
  and and_3 (and_3_out, comp_5_c, comp_6_c);
  and and_4 (and_4_out, comp_7_c, comp_8_c);
  and and_5 (and_5_out, and_1_out, and_2_out);
  and and_6 (and_6_out, and_3_out, and_4_out);
  and and_7 (out_2, and_5_out, and_6_out);
endmodule

module MUL_Overflow (
  input  a,
  input  b,
  input  c,
  input  d,
  input  [2:0] OP,
  output out_6
);

  wire com_overflow_1_s, dec_overflow_1_a0, dec_overflow_1_a1, mul_2_1_b_1_s, mul_2_1_b_2_s, mul_2_1_b_3_s;

  MUL_2_1_b mul_2_1_b_1 (.a(a), .b(b), .c(dec_overflow_1_a0), .s(mul_2_1_b_1_s));
  MUL_2_1_b mul_2_1_b_2 (.a(c), .b(d), .c(dec_overflow_1_a0), .s(mul_2_1_b_2_s));
  DEC_Overflow dec_overflow_1 (.a(OP[2]), .b(OP[1]), .c(OP[0]), .a0(dec_overflow_1_a0), .a1(dec_overflow_1_a1));
  MUL_2_1_b mul_2_1_b_3 (.a(mul_2_1_b_1_s), .b(mul_2_1_b_2_s), .c(dec_overflow_1_a1), .s(mul_2_1_b_3_s));
  COM_Overflow com_overflow_1 (.a(OP[2]), .b(OP[1]), .c(OP[0]), .s(com_overflow_1_s));
  AND and_1 (.a(mul_2_1_b_3_s), .b(com_overflow_1_s), .s(out_6));
endmodule

module DEC_Overflow (
  input  a,
  input  b,
  input  c,
  output a0,
  output a1
);

  wire and_1_out, not_1_out;

  not not_1 (not_1_out, a);
  and and_1 (and_1_out, not_1_out, c);
  or or_1 (a0, and_1_out, b);

  assign a1 = a;
endmodule

module COM_Overflow (
  input  a,
  input  b,
  input  c,
  output s
);

  wire and_1_out, and_2_out, and_3_out, not_1_out, not_2_out, not_3_out, not_4_out;

  not not_1 (not_1_out, a);
  not not_2 (not_2_out, b);
  not not_3 (not_3_out, b);
  not not_4 (not_4_out, c);
  and and_1 (and_1_out, not_1_out, not_2_out);
  and and_2 (and_2_out, not_3_out, c);
  and and_3 (and_3_out, a, b, not_4_out);
  or or_1 (s, and_1_out, and_2_out, and_3_out);
endmodule
